# Fritzing sketch GPSDataLogger (saved by Fritzing 0.9.2b)
breadboards: 1

parts:
  Part1 = Arduino Uno (Rev3)
  S1 = Momentary Switch [package=ksa_sealed_tac_switch]
  U1 = SWITCH_SPDT [package=kps-1290]
  U2 = SWITCH_SPDT [package=kps-1290]
  U3 = SWITCH_SPDT [package=kps-1290]
  LED2 = smd LED [color="White (4500K)" package="0603 [SMD]"]
  LED8 = smd LED [color="White (4500K)" package="0603 [SMD]"]
  R7 = Resistor [tolerance=±5% resistance=10k package="2010 [SMD]"]
  R8 = Resistor [tolerance=±5% resistance=10k package="2010 [SMD]"]
  R9 = Resistor [tolerance=±5% resistance=10k package="2010 [SMD]"]
  R10 = Resistor [tolerance=±5% resistance=220 package="2010 [SMD]"]
  R11 = Resistor [tolerance=±5% resistance=220 package="2010 [SMD]"]
  LED10 = smd LED [color="Red (633nm)" package="0603 [SMD]"]
  LED11 = smd LED [color="Yellow (585nm)" package="0603 [SMD]"]
  LED12 = smd LED [color="Green (555nm)" package="0603 [SMD]"]
  R4 = Resistor [tolerance=±5% resistance=220 package="2010 [SMD]"]
  LED13 = smd LED [color="White (4500K)" package="0603 [SMD]"]
  R13 = Resistor [tolerance=±5% resistance=10k package="2010 [SMD]"]
  R14 = Photocell (LDR) [package=THT]

nets:
  N1: Part1.A0, R10.Pin_1
  N2: Part1.A1, R4.Pin_1
  N3: Part1.A2, R11.Pin_1
  N4: Part1.A5/SCL, R13.Pin_0, R14.pin_1
  N5: Part1.D3_PWM, U1.P, R7.Pin_1
  N6: Part1.D5_PWM, S1.3
  N7: Part1.D6_PWM, U3.P, R9.Pin_1
  N8: Part1.D7, U2.P, R8.Pin_1
  N9: Part1.5V, R14.pin_0
  N10: Part1.GND, S1.1, LED2.cathode, LED8.cathode, LED10.cathode, LED11.cathode, LED12.cathode, LED13.cathode, R13.Pin_1
  N11: U1.O, U2.O, U3.O
  N12: U1.S, U2.S, U3.S
  N13: LED2.anode, R9.Pin_0
  N14: LED8.anode, R7.Pin_0
  N15: R8.Pin_0, LED13.anode
  N16: R10.Pin_0, LED10.anode
  N17: R11.Pin_0, LED12.anode
  N18: LED11.anode, R4.Pin_0

notes:
  Adafruit Ultimate GPS
  VIN - 5V
  GND - GND
  RX - Pin 9
  TX - Pin 8
  Micro SD Slot
  CS - Pin 4
  SCK - Pin 13
  MOSI - Pin 11
  MISO - Pin 12
  VCC - 5V
  GND - GND
